// Digital circuit control_finca.dig as structural Verilog
module control_finca (
  input  I0_2,
  input  I0_3,
  input  I0_4,
  input  I0_1,
  output Q0_1,
  output Q0_2,
  output Q0_4,
  output Q0_3,
  output Q0_5,
  output Q0_6,
  output Q0_7
);

  wire not_2_out, nP, or_1_out, or_2_out;

  not not_1 (nP, I0_4);
  not not_2 (not_2_out, I0_1);
  or or_1 (or_1_out, I0_1, I0_2);
  not not_3 (Q0_3, I0_2);
  or or_2 (or_2_out, I0_3, not_2_out);
  and and_1 (Q0_2, or_1_out, nP);
  and and_2 (Q0_1, or_2_out, nP, I0_2);

  assign Q0_4 = Q0_2;
  assign Q0_5 = I0_1;
  assign Q0_6 = I0_3;
  assign Q0_7 = I0_4;
endmodule

/* Test case:
I0_4 I0_3 I0_2 I0_1 Q0_7 Q0_6 Q0_5 Q0_4 Q0_3 Q0_2 Q0_1
0 0 0 0 0 0 0 0 1 0 0
0 0 0 1 0 0 1 1 1 1 0
0 0 1 0 0 0 0 1 0 1 1
0 0 1 1 0 0 1 1 0 1 0
0 1 0 0 0 1 0 0 1 0 0
0 1 0 1 0 1 1 1 1 1 0
0 1 1 0 0 1 0 1 0 1 1
0 1 1 1 0 1 1 1 0 1 1
1 0 0 0 1 0 0 0 1 0 0
1 0 0 1 1 0 1 0 1 0 0
1 0 1 0 1 0 0 0 0 0 0
1 0 1 1 1 0 1 0 0 0 0
1 1 0 0 1 1 0 0 1 0 0
1 1 0 1 1 1 1 0 1 0 0
1 1 1 0 1 1 0 0 0 0 0
1 1 1 1 1 1 1 0 0 0 0
*/
