// Digital circuit dominio_fisico_contactos.dig as structural Verilog
module dominio_fisico_contactos (
  input  I01,
  input  I02,
  input  I03,
  input  I04
);

  wire K2, relay_1_p4, relay_2_p4, relay_3_p5, relay_4_p3, relay_5_p3, relay_6_p3, relay_7_p2, relay_8_p4,
       relay_11_p5;

  // Relay #(.relayNormallyClosed("true")) relay_1: pin names not known; wires that end beside it: I04, 1'b1, 1'b0, relay_1_p4
  // Relay #(.relayNormallyClosed("true")) relay_2: pin names not known; wires that end beside it: I04, 1'b1, 1'b0, relay_2_p4
  // Relay #(.relayNormallyClosed("true")) relay_3: pin names not known; wires that end beside it: I02, 1'b1, K2, 1'b0, relay_3_p5, 1'b0
  // Relay relay_4: pin names not known; wires that end beside it: 1'b1, I01, relay_4_p3, 1'b0
  // Relay relay_5: pin names not known; wires that end beside it: 1'b1, I03, relay_5_p3, 1'b0
  // Relay relay_6: pin names not known; wires that end beside it: 1'b1, I04, relay_6_p3, 1'b0
  // Relay relay_7: pin names not known; wires that end beside it: 1'b1, relay_7_p2
  // Relay relay_8: pin names not known; wires that end beside it: I02, relay_1_p4, 1'b0, relay_8_p4
  // Relay relay_9: pin names not known; wires that end beside it: I01, relay_2_p4, I02, 1'b0, K2, 1'b0
  // Relay relay_10: pin names not known; wires that end beside it: relay_2_p4, K2
  // Relay relay_11: pin names not known; wires that end beside it: I03, relay_8_p4, I01, 1'b0, relay_11_p5, 1'b0
  // Relay #(.relayNormallyClosed("true")) relay_12: pin names not known; wires that end beside it: relay_8_p4, relay_11_p5
  // Relay K1: pin names not known; wires that end beside it: relay_11_p5, 1'b0
  // Relay K2: pin names not known; wires that end beside it: K2, 1'b0
  LightBulb lightbulb_1 (.A(relay_3_p5), .B(1'b0));
  LightBulb lightbulb_2 (.A(relay_4_p3), .B(1'b0));
  LightBulb lightbulb_3 (.A(relay_5_p3), .B(1'b0));
  LightBulb lightbulb_4 (.A(relay_6_p3), .B(1'b0));
  LightBulb lightbulb_5 (.A(relay_7_p2), .B(1'b0));

  // Notes on the sheet:
  //   I01: sensor de red
  //   I02: sensor de batería
  //   I03: sensor de luz
  //   I04: paro de emergencia
  //   VDD = fuente de control
  //   Sensores y mando: clic en la entrada para cambiar 0/1
  //   sensor de red
  //   sensor de batería
  //   sensor de luz
  //   paro de emergencia
  //   Dominio físico inicial: red de control con contactos (lógica cableada)
  //   Q0.1  relé conmutador K1
  //   Q0.2  relé energizador K2
  //   Q0.3  piloto batería descargada
  //   Q0.4  piloto casa energizada
  //   Q0.5  piloto red disponible
  //   Q0.6  piloto radiación solar
  //   Q0.7  piloto paro activo
  //   tierra = retorno
endmodule
